// Logisim project 1KB ram chip using 256B ram chips.circ as structural Verilog: 1 circuit, main circuit main
module main (
  input  [1:0] Selection_Bit,
  input  CLEAR,
  input  [7:0] Address_bit,
  input  WR,
  input  CLOCK,
  input  RD,
  input  [7:0] INPUT_DATA_BIT,
  input  in_8,
  output [7:0] OUTPUT_DATA_BIT
);

  wire decoder_1_out0, decoder_1_out1, decoder_1_out2, decoder_1_out3;

  Decoder #(.select(2)) decoder_1 (
    .out0(decoder_1_out0), .out1(decoder_1_out1), .out2(decoder_1_out2), .out3(decoder_1_out3),
    .sel(Selection_Bit), .en(in_8));
  RAM #(.bus("separate")) ram_1 (
    .addr(Address_bit), .din(INPUT_DATA_BIT), .data(OUTPUT_DATA_BIT), .str(WR), .sel(decoder_1_out0),
    .clk(CLOCK), .ld(RD), .clr(CLEAR));
  RAM #(.bus("separate")) ram_2 (
    .addr(Address_bit), .din(INPUT_DATA_BIT), .data(OUTPUT_DATA_BIT), .str(WR), .sel(decoder_1_out1),
    .clk(CLOCK), .ld(RD), .clr(CLEAR));
  RAM #(.bus("separate")) ram_3 (
    .addr(Address_bit), .din(INPUT_DATA_BIT), .data(OUTPUT_DATA_BIT), .str(WR), .sel(decoder_1_out2),
    .clk(CLOCK), .ld(RD), .clr(CLEAR));
  RAM #(.bus("separate")) ram_4 (
    .addr(Address_bit), .din(INPUT_DATA_BIT), .data(OUTPUT_DATA_BIT), .str(WR), .sel(decoder_1_out3),
    .clk(CLOCK), .ld(RD), .clr(CLEAR));

  // Notes on the sheet:
  //   1KB RAM CHIP
endmodule
