// Logisim project 1kb ram chip using 128x8 ram and 512x8 rom chip.circ as structural Verilog: 1 circuit, main circuit main
module main (
  input  RD,
  input  WR,
  input  [7:0] D7_D0,
  input  CLR,
  input  [9:0] in_5,
  output [7:0] D7_D0_2
);

  wire clock_1_out, decoder_1_out0, decoder_1_out1, decoder_1_out2, decoder_1_out3, not_1_out;

  Decoder #(.select(2)) decoder_1 (
    .out0(decoder_1_out0), .out1(decoder_1_out1), .out2(decoder_1_out2), .out3(decoder_1_out3),
    .sel(in_5[8:7]), .en(not_1_out));
  not not_1 (not_1_out, in_5[9]);
  Clock clock_1 (.out(clock_1_out));
  RAM #(.addrWidth(7), .bus("separate")) ram_1 (
    .addr(in_5[6:0]), .din(D7_D0), .data(D7_D0_2), .str(WR), .sel(decoder_1_out0), .clk(clock_1_out),
    .ld(RD), .clr(CLR));
  RAM #(.addrWidth(7), .bus("separate")) ram_2 (
    .addr(in_5[6:0]), .din(D7_D0), .data(D7_D0_2), .str(WR), .sel(decoder_1_out1), .clk(clock_1_out),
    .ld(RD), .clr(CLR));
  RAM #(.addrWidth(7), .bus("separate")) ram_3 (
    .addr(in_5[6:0]), .din(D7_D0), .data(D7_D0_2), .str(WR), .sel(decoder_1_out2), .clk(clock_1_out),
    .ld(RD), .clr(CLR));
  RAM #(.addrWidth(7), .bus("separate")) ram_4 (
    .addr(in_5[6:0]), .din(D7_D0), .data(D7_D0_2), .str(WR), .sel(decoder_1_out3), .clk(clock_1_out),
    .ld(RD), .clr(CLR));
  ROM #(.addrWidth(9)) rom_1 (.addr(in_5[8:0]), .data(D7_D0_2), .sel(in_5[9]));

  // Notes on the sheet:
  //   A9-A0
  //   INPUT
  //   CLK
  //   contents of rom_1 (hex, n*v repeats v):
  //   2 5 d
  //   OUTPUT
endmodule
