// Logisim project 256B ram chip using two  128B ram chips.circ as structural Verilog: 1 circuit, main circuit main
module main (
  input  Selection_Bit,
  input  [6:0] Address_Bit,
  input  [7:0] Input_Data_Bit,
  input  WR,
  input  RD,
  input  Clear,
  output [7:0] Output_Data_Bit
);

  wire clock_1_out, not_1_out;

  not not_1 (not_1_out, Selection_Bit);
  Clock clock_1 (.out(clock_1_out));
  RAM #(.addrWidth(7), .bus("separate")) ram_1 (
    .addr(Address_Bit), .din(Input_Data_Bit), .data(Output_Data_Bit), .str(WR), .sel(not_1_out),
    .clk(clock_1_out), .ld(RD), .clr(Clear));
  RAM #(.addrWidth(7), .bus("separate")) ram_2 (
    .addr(Address_Bit), .din(Input_Data_Bit), .data(Output_Data_Bit), .str(WR), .sel(Selection_Bit),
    .clk(clock_1_out), .ld(RD), .clr(Clear));

  // Notes on the sheet:
  //   A7
  //   A6-A0
  //   D7-D0
  //   Clock
  //   256B RAM CHIP
  //   D7-D0
endmodule
