// Logisim project 512x16 ram chip by using 128x8 ram chip.circ as structural Verilog: 1 circuit, main circuit main
module main (
  input  CLR,
  input  RD,
  input  WR,
  input  [7:0] D15_D8,
  input  [7:0] D7_D0,
  input  [8:0] in_6,
  input  in_7,
  output [7:0] D15_D8_2,
  output [7:0] D7_D0_2
);

  wire clock_1_out, decoder_1_out0, decoder_1_out1, decoder_1_out2, decoder_1_out3;

  Decoder #(.select(2)) decoder_1 (
    .out0(decoder_1_out0), .out1(decoder_1_out1), .out2(decoder_1_out2), .out3(decoder_1_out3),
    .sel(in_6[8:7]), .en(in_7));
  RAM #(.addrWidth(7), .bus("separate")) ram_1 (
    .addr(in_6[6:0]), .din(D15_D8), .data(D15_D8_2), .str(WR), .sel(decoder_1_out0), .clk(clock_1_out),
    .ld(RD), .clr(CLR));
  RAM #(.addrWidth(7), .bus("separate")) ram_2 (
    .addr(in_6[6:0]), .din(D15_D8), .data(D15_D8_2), .str(WR), .sel(decoder_1_out1), .clk(clock_1_out),
    .ld(RD), .clr(CLR));
  RAM #(.addrWidth(7), .bus("separate")) ram_3 (
    .addr(in_6[6:0]), .din(D15_D8), .data(D15_D8_2), .str(WR), .sel(decoder_1_out2), .clk(clock_1_out),
    .ld(RD), .clr(CLR));
  RAM #(.addrWidth(7), .bus("separate")) ram_4 (
    .addr(in_6[6:0]), .din(D15_D8), .data(D15_D8_2), .str(WR), .sel(decoder_1_out3), .clk(clock_1_out),
    .ld(RD), .clr(CLR));
  Clock clock_1 (.out(clock_1_out));
  RAM #(.addrWidth(7), .bus("separate")) ram_5 (
    .addr(in_6[6:0]), .din(D7_D0), .data(D7_D0_2), .str(WR), .sel(decoder_1_out0), .clk(clock_1_out),
    .ld(RD), .clr(CLR));
  RAM #(.addrWidth(7), .bus("separate")) ram_6 (
    .addr(in_6[6:0]), .din(D7_D0), .data(D7_D0_2), .str(WR), .sel(decoder_1_out1), .clk(clock_1_out),
    .ld(RD), .clr(CLR));
  RAM #(.addrWidth(7), .bus("separate")) ram_7 (
    .addr(in_6[6:0]), .din(D7_D0), .data(D7_D0_2), .str(WR), .sel(decoder_1_out2), .clk(clock_1_out),
    .ld(RD), .clr(CLR));
  RAM #(.addrWidth(7), .bus("separate")) ram_8 (
    .addr(in_6[6:0]), .din(D7_D0), .data(D7_D0_2), .str(WR), .sel(decoder_1_out3), .clk(clock_1_out),
    .ld(RD), .clr(CLR));

  // Notes on the sheet:
  //   A8-A0
  //   INPUT
  //   CLK
  //   OUTPUT
endmodule
