// Logisim project Design a 2KB RAM chip by using above mention 1KB RAM chip.circ as structural Verilog: 1 circuit, main circuit main
module main (
  input  [10:0] in_1,
  input  [7:0] Input_Data_Bit,
  input  WR,
  input  RD,
  input  CLR,
  output [7:0] Output_Data_Bit
);

  wire clock_1_out, not_1_out;

  not not_1 (not_1_out, in_1[10]);
  Clock clock_1 (.out(clock_1_out));
  _1KB_ram_chip_using_256B_ram_chips_main main_1 (
    .in_8(not_1_out), .OUTPUT_DATA_BIT(Output_Data_Bit), .Selection_Bit(in_1[9:8]), .Address_bit(in_1[7:0]),
    .WR(WR), .RD(RD), .INPUT_DATA_BIT(Input_Data_Bit), .CLEAR(CLR), .CLOCK(clock_1_out));
  _1KB_ram_chip_using_256B_ram_chips_main main_2 (
    .in_8(in_1[10]), .OUTPUT_DATA_BIT(Output_Data_Bit), .Selection_Bit(in_1[9:8]), .Address_bit(in_1[7:0]),
    .WR(WR), .RD(RD), .INPUT_DATA_BIT(Input_Data_Bit), .CLEAR(CLR), .CLOCK(clock_1_out));

  // Notes on the sheet:
  //   A10-A0
  //   D7-D0
  //   CLK
  //   D7-D0
endmodule
