// Logisim project 4 bit -arithmetic- unit.circ as structural Verilog: 1 circuit, main circuit main
module main (
  input  Cin,
  input  [1:0] S1,
  input  A0,
  input  B0,
  input  in_5,
  input  in_6,
  input  A1,
  input  B1,
  input  in_9,
  input  in_10,
  input  A2,
  input  B2,
  input  in_13,
  input  in_14,
  input  A3,
  input  B3,
  input  in_17,
  input  in_18,
  output R0,
  output R1,
  output R2,
  output R3,
  output Cout
);

  wire multiplexer_1_out, multiplexer_2_out, multiplexer_3_out, multiplexer_4_out, not_1_out, not_2_out,
       not_3_out, not_4_out;

  not not_1 (not_1_out, B0);
  not not_2 (not_2_out, B1);
  not not_3 (not_3_out, B2);
  not not_4 (not_4_out, B3);
  Multiplexer #(.select(2), .enable("false")) multiplexer_1 (
    .in0(B0), .in1(not_1_out), .in2(in_5), .in3(in_6), .out(multiplexer_1_out), .sel(S1));
  Multiplexer #(.select(2), .enable("false")) multiplexer_2 (
    .in0(B1), .in1(not_2_out), .in2(in_9), .in3(in_10), .out(multiplexer_2_out), .sel(S1));
  Multiplexer #(.select(2), .enable("false")) multiplexer_3 (
    .in0(B2), .in1(not_3_out), .in2(in_13), .in3(in_14), .out(multiplexer_3_out), .sel(S1));
  Multiplexer #(.select(2), .enable("false")) multiplexer_4 (
    .in0(B3), .in1(not_4_out), .in2(in_17), .in3(in_18), .out(multiplexer_4_out), .sel(S1));
  Ripple_Carry_Adder__main main_1 (
    .Cout(Cout), .Cin(Cin), .B3(multiplexer_4_out), .A3(A3), .B2(multiplexer_3_out), .A2(A2),
    .B1(multiplexer_2_out), .A1(A1), .B0(multiplexer_1_out), .A0(A0), .S3(R3), .S2(R2), .S1(R1), .S0(R0));

  // Notes on the sheet:
  //   S0
  //   Y0
  //   Y1
  //   Y2
  //   Y3
  //   4 Bit Arithmetic Unit
endmodule
