// Logisim project 4 bit adder-subtractor composite unit.circ as structural Verilog: 1 circuit, main circuit main
module main (
  input  B3,
  input  B2,
  input  B1,
  input  B0,
  input  A3,
  input  A2,
  input  A1,
  input  A0,
  input  Cin,
  output Cout,
  output S3,
  output S2,
  output S1,
  output S0
);

  wire main_2_cout, main_3_cout, main_4_cout, xor_1_out, xor_2_out, xor_3_out, xor_4_out;

  xor xor_1 (xor_1_out, Cin, B3);
  full_adder_main main_1 (.A(xor_1_out), .B(A3), .Cin(main_2_cout), .S(S3), .Cout(Cout));
  xor xor_2 (xor_2_out, Cin, B2);
  full_adder_main main_2 (.A(xor_2_out), .B(A2), .Cin(main_3_cout), .S(S2), .Cout(main_2_cout));
  xor xor_3 (xor_3_out, Cin, B1);
  full_adder_main main_3 (.A(xor_3_out), .B(A1), .Cin(main_4_cout), .S(S1), .Cout(main_3_cout));
  xor xor_4 (xor_4_out, Cin, B0);
  full_adder_main main_4 (.A(xor_4_out), .B(A0), .Cin(Cin), .S(S0), .Cout(main_4_cout));

  // Notes on the sheet:
  //   Full Adder 4
  //   Full Adder 3
  //   4 Bit Adder-Subtractor Composite Unit
  //   Full Adder 2
  //   Full Adder 1
  //   SW
endmodule
