// Logisim project Binary_4_bit_decrementer_circuit.circ as structural Verilog: 1 circuit, main circuit main
module main (
  input  A3,
  input  A2,
  input  A1,
  input  A0,
  input  Cin,
  output Cout,
  output S3,
  output S2,
  output S1,
  output S0
);

  wire main_2_cout, main_3_cout, main_4_cout;

  full_adder_main main_1 (.A(A3), .B(1'b1), .Cin(main_2_cout), .S(S3), .Cout(Cout));
  full_adder_main main_2 (.A(A2), .B(1'b1), .Cin(main_3_cout), .S(S2), .Cout(main_2_cout));
  full_adder_main main_3 (.A(A1), .B(1'b1), .Cin(main_4_cout), .S(S1), .Cout(main_3_cout));
  full_adder_main main_4 (.A(A0), .B(1'b1), .Cin(Cin), .S(S0), .Cout(main_4_cout));

  // Notes on the sheet:
  //   Full Adder 4
  //   C2
  //   Full Adder 3
  //   1
  //   C1
  //   Binary 4 Bit Decrementer Circuit
  //   Full Adder 2
  //   C0
  //   Full Adder 1
endmodule
