// Logisim project Binary_4_bit_incrementer_circuit.circ as structural Verilog: 1 circuit, main circuit main
module main (
  input  A3,
  input  A2,
  input  A1,
  input  A0,
  output Cout,
  output S3,
  output S2,
  output S1,
  output S0
);

  wire main_2_out_4, main_3_out_4, main_4_out_4;

  half_adder_for_binary4bit_incremt_circuit_main main_1 (.in_1(A3), .in_2(main_2_out_4), .out_3(S3), .out_4(Cout));
  half_adder_for_binary4bit_incremt_circuit_main main_2 (
    .in_1(A2), .in_2(main_3_out_4), .out_3(S2), .out_4(main_2_out_4));
  half_adder_for_binary4bit_incremt_circuit_main main_3 (
    .in_1(A1), .in_2(main_4_out_4), .out_3(S1), .out_4(main_3_out_4));
  half_adder_for_binary4bit_incremt_circuit_main main_4 (.in_1(A0), .in_2(1'b1), .out_3(S0), .out_4(main_4_out_4));

  // Notes on the sheet:
  //   Half Adder 4
  //   C2
  //   Half Adder 3
  //   Binary 4 Bit Incrementer Circuit
  //   C1
  //   Half Adder 2
  //   C0
  //   1
  //   Half Adder 1
endmodule
