// Logisim project CarryLookAheadAdder.circ as structural Verilog: 1 circuit, main circuit main
module main (
  input  B3,
  input  A3,
  input  B2,
  input  A2,
  input  B1,
  input  A1,
  input  B0,
  input  A0,
  input  in_9,
  output out_10,
  output out_11,
  output out_12,
  output out_13,
  output out_14
);

  wire main_1_out_5, main_1_out_6, main_2_out_5, main_2_out_6, main_3_c1, main_3_c2, main_3_c3, main_4_out_5,
       main_4_out_6, main_5_out_5, main_5_out_6;

  LFA_main main_1 (.in_1(A3), .in_2(B3), .in_3(main_3_c3), .out_4(out_10), .out_5(main_1_out_5), .out_6(main_1_out_6));
  LFA_main main_2 (.in_1(A2), .in_2(B2), .in_3(main_3_c2), .out_4(out_11), .out_5(main_2_out_5), .out_6(main_2_out_6));
  CLG_main main_3 (
    .C1(main_3_c1), .C2(main_3_c2), .C3(main_3_c3), .Cout(out_14), .G0(main_5_out_6), .P0(main_5_out_5),
    .C0(in_9), .G1(main_4_out_6), .P1(main_4_out_5), .G2(main_2_out_6), .P2(main_2_out_5), .G3(main_1_out_6),
    .P3(main_1_out_5));
  LFA_main main_4 (.in_1(A1), .in_2(B1), .in_3(main_3_c1), .out_4(out_12), .out_5(main_4_out_5), .out_6(main_4_out_6));
  LFA_main main_5 (.in_1(A0), .in_2(B0), .in_3(in_9), .out_4(out_13), .out_5(main_5_out_5), .out_6(main_5_out_6));

  // Notes on the sheet:
  //   Carry Look-Ahead Adder
endmodule
