// Logisim project LFA.circ as structural Verilog: 1 circuit, main circuit main
module main (
  input  in_1,
  input  in_2,
  input  in_3,
  output out_4,
  output out_5,
  output out_6
);

  xor xor_1 (out_5, in_1, in_2);
  and and_1 (out_6, in_1, in_2);
  xor xor_2 (out_4, out_5, in_3);
endmodule
