// Logisim project Ripple_Carry_Adder_.circ as structural Verilog: 1 circuit, main circuit main
module main (
  input  B3,
  input  A3,
  input  B2,
  input  A2,
  input  B1,
  input  A1,
  input  B0,
  input  A0,
  input  Cin,
  output Cout,
  output S3,
  output S2,
  output S1,
  output S0
);

  wire main_2_cout, main_3_cout, main_4_cout;

  full_adder_main main_1 (.A(B3), .B(A3), .Cin(main_2_cout), .S(S3), .Cout(Cout));
  full_adder_main main_2 (.A(B2), .B(A2), .Cin(main_3_cout), .S(S2), .Cout(main_2_cout));
  full_adder_main main_3 (.A(B1), .B(A1), .Cin(main_4_cout), .S(S1), .Cout(main_3_cout));
  full_adder_main main_4 (.A(B0), .B(A0), .Cin(Cin), .S(S0), .Cout(main_4_cout));

  // Notes on the sheet:
  //   Full Adder 4
  //   C2
  //   Full Adder 3
  //   Ripple Carry Adder
  //   C1
  //   Full Adder 2
  //   C0
  //   Full Adder 1
endmodule
