// Logisim project full subtractor.circ as structural Verilog: 1 circuit, main circuit main
module main (
  input  A,
  input  B,
  input  Bin,
  input  A_2,
  input  B_2,
  input  Bin_2,
  output D,
  output Bout,
  output out_9,
  output out_10
);

  wire and_1_out, and_2_out, main_1_br, main_1_d, main_2_br, not_1_out, not_2_out, xor_1_out;

  not not_1 (not_1_out, A);
  xor xor_1 (xor_1_out, A, B);
  not not_2 (not_2_out, xor_1_out);
  xor xor_2 (D, xor_1_out, Bin);
  and and_1 (and_1_out, B, not_1_out);
  half_subtractor_main main_1 (.A(A_2), .B(B_2), .D(main_1_d), .Br(main_1_br));
  and and_2 (and_2_out, not_2_out, Bin);
  or or_1 (Bout, and_2_out, and_1_out);
  half_subtractor_main main_2 (.A(main_1_d), .B(Bin_2), .D(out_9), .Br(main_2_br));
  or or_2 (out_10, main_2_br, main_1_br);

  // Notes on the sheet:
  //   A XOR B
  //   A'B
  //   Full Subtractor
  //   (A XOR B)' AND Bin
  //   A XOR B XOR Bin
  //   A'B OR ((A XOR B)' AND Bin)
endmodule
